# Fritzing sketch pritz project ph reader (saved by Fritzing 0.9.3b)
circuit board: 7cm x 5cm
breadboards: 1

parts:
  Componente1 = Arduino Nano (Rev3.0)
  pH_Circuit1 = pH Circuit
  U1 = LCD-16X2 [package=lcd-16x2_nosilk]
  U2 = POT [package=3362u]
  R1 = Resistor [tolerance=±5% resistance=220 package="1206 [SMD]"]

nets:
  GND: Componente1.GND, pH_Circuit1.GND, U1.VSS, U1.R_W, U1.K, U2.E
  N1: Componente1.D2, U1.DB7
  N2: Componente1.D3, U1.DB6
  N3: Componente1.D4, U1.DB5
  N4: Componente1.D5, U1.DB4
  N5: Componente1.D11/MOSI, U1.E
  N6: Componente1.D12/MISO, U1.RS
  5V: Componente1.5V, pH_Circuit1.Vcc, U1.VDD, U2.A, R1.Pin_0
  N7: Componente1.A0, pH_Circuit1.RX
  N8: U1.VO, U2.S
  N9: U1.A, R1.Pin_1

custom parts:
  pH Circuit: Ph circuit designs that are available on the Internet today are antiquated and use a significant number of overly complex analog components. Atlas Scientific has reinvented and refined the pH Circuit of yesteryear. The Atlas Scientific pH Circuit is our fifth generation pH Circuit. The Atlas Scientific pH Circuit enables the engineer to easily incorporate scientific grade pH monitoring into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

// code stored in the sketch: main.ino
// pHRead.ino

#include <LiquidCrystal.h>
LiquidCrystal lcd(12, 11, 5, 4, 3, 2);

// Constants:-
const byte pHpin = A0;// Connect the sensor's Po output to analogue pin 0.

// Variables:-
float Po;

void setup()
{
Serial.begin(9600);
lcd.begin(16, 2);             // set up the LCD's number of columns and rows:
lcd.print("hello, world!");   // Print a message to the LCD.
}

void loop()
{
  Po = (1023 - analogRead(pHpin)) / 73.07; // Read and reverse the analogue input value from the pH sensor then scale 0-14.
  Serial.println(Po, 2);// Print the result in the serial monitor.
  lcd.setCursor(0, 0);
  lcd.print("PH = ");
  lcd.setCursor(5, 0);
  lcd.print(Po,2);
  lcd.setCursor(9, 0);
  lcd.print("       ");
  lcd.setCursor(0, 1);
  lcd.print("                ");
  
  delay(1000);// Take 1 reading per second.
  
}
